# Fritzing sketch 01_servoMotor (saved by Fritzing 0.9.3b)

parts:
  S1 = H-Bridge with L298N
  Εξάρτημα1 = Arduino Uno (Rev3)
  M2 = DC Motor
  M3 = DC Motor
  VCC1 = Battery block 9V
  S2 = SPST Switch [package=switch-spdt_kit]
  J1 = Basic Servo

nets:
  12V: S1.12V, Εξάρτημα1.VIN, S2.S
  GND: S1.GND, Εξάρτημα1.GND, VCC1.-, J1.gnd
  N1: S1.ENA, S1.ENA-5V
  N2: S1.IN1, Εξάρτημα1.D11_PWM/MOSI
  N3: S1.IN2, Εξάρτημα1.D10_PWM/SS
  N4: S1.IN3, Εξάρτημα1.D8
  N5: S1.IN4, Εξάρτημα1.D9_PWM
  N6: S1.ENB, S1.ENB-5V
  N7: S1.M1-01, M2.pin_2
  N8: S1.M1-02, M2.pin_1
  N9: S1.M2-01, M3.pin_2
  N10: S1.M2-02, M3.pin_1
  N11: Εξάρτημα1.D2, J1.pulse
  5V: Εξάρτημα1.5V, J1.vcc
  N12: VCC1.+, S2.P

custom parts:
  H-Bridge with L298N: h-bridge
